// Logisim project 4 Bit binary adder substractor.circ as structural Verilog: 1 circuit, main circuit main
module main (
  input  B3,
  input  A3,
  input  B2,
  input  A2,
  input  B1,
  input  A1,
  input  B0,
  input  A0,
  input  in_9
);

  wire adder_1_cout, adder_1_out, adder_2_cout, adder_2_out, adder_3_cout, adder_3_out, adder_4_cout,
       adder_4_out, xor_1_out, xor_2_out, xor_3_out, xor_4_out;

  xor xor_1 (xor_1_out, in_9, B3);
  LED led_1 (.in(adder_1_cout));
  Adder #(.width(1)) adder_1 (.a(A3), .b(xor_1_out), .out(adder_1_out), .cin(adder_2_cout), .cout(adder_1_cout));
  LED led_2 (.in(adder_1_out));
  xor xor_2 (xor_2_out, in_9, B2);
  Adder #(.width(1)) adder_2 (.a(A2), .b(xor_2_out), .out(adder_2_out), .cin(adder_3_cout), .cout(adder_2_cout));
  LED led_3 (.in(adder_2_out));
  xor xor_3 (xor_3_out, in_9, B1);
  Adder #(.width(1)) adder_3 (.a(A1), .b(xor_3_out), .out(adder_3_out), .cin(adder_4_cout), .cout(adder_3_cout));
  LED led_4 (.in(adder_3_out));
  xor xor_4 (xor_4_out, in_9, B0);
  Adder #(.width(1)) adder_4 (.a(A0), .b(xor_4_out), .out(adder_4_out), .cin(in_9), .cout(adder_4_cout));
  LED led_5 (.in(adder_4_out));

  // Notes on the sheet:
  //   S3
  //   S2
  //   4 Bit binary adder substractor
  //   S1
  //   S0
endmodule
