// Logisim project 4 Bit binary adder.circ as structural Verilog: 1 circuit, main circuit main
module main (
  input  B3,
  input  A3,
  input  B2,
  input  A2,
  input  B1,
  input  A1,
  input  B0,
  input  A0,
  input  C0
);

  wire adder_1_cout, adder_1_out, adder_2_cout, adder_2_out, adder_3_cout, adder_3_out, adder_4_cout,
       adder_4_out;

  LED led_1 (.in(adder_1_cout));
  Adder #(.width(1)) adder_1 (.a(A3), .b(B3), .out(adder_1_out), .cin(adder_2_cout), .cout(adder_1_cout));
  LED led_2 (.in(adder_1_out));
  Adder #(.width(1)) adder_2 (.a(A2), .b(B2), .out(adder_2_out), .cin(adder_3_cout), .cout(adder_2_cout));
  LED led_3 (.in(adder_2_out));
  Adder #(.width(1)) adder_3 (.a(A1), .b(B1), .out(adder_3_out), .cin(adder_4_cout), .cout(adder_3_cout));
  LED led_4 (.in(adder_3_out));
  Adder #(.width(1)) adder_4 (.a(A0), .b(B0), .out(adder_4_out), .cin(C0), .cout(adder_4_cout));
  LED led_5 (.in(adder_4_out));

  // Notes on the sheet:
  //   C4
  //   C3
  //   S3
  //   C2
  //   S2
  //   4 Bit binary adder
  //   C1
  //   S1
  //   S0
endmodule
