// Logisim project 4 Bit bus line with three state buffer.circ as structural Verilog: 1 circuit, main circuit main
module main (
  input  A0,
  input  in_2,
  input  in_3,
  input  in_4,
  input  B0,
  input  in_6,
  input  in_7,
  input  in_8,
  input  C0,
  input  in_10,
  input  in_11,
  input  in_12,
  input  D0,
  input  in_14,
  input  in_15,
  input  in_16,
  input  [1:0] in_17
);

  wire controlled_buffer_1_out, controlled_buffer_5_out, controlled_buffer_9_out, controlled_buffer_13_out,
       decoder_1_out0, decoder_1_out1, decoder_1_out2, decoder_1_out3;

  assign controlled_buffer_1_out = decoder_1_out0 ? A0 : 1'bz;  // Controlled_Buffer controlled_buffer_1
  assign controlled_buffer_1_out = decoder_1_out1 ? B0 : 1'bz;  // Controlled_Buffer controlled_buffer_2
  Decoder #(.select(2)) decoder_1 (
    .out0(decoder_1_out0), .out1(decoder_1_out1), .out2(decoder_1_out2), .out3(decoder_1_out3), .sel(in_17));  // open: en
  LED led_1 (.in(controlled_buffer_1_out));
  assign controlled_buffer_1_out = decoder_1_out2 ? C0 : 1'bz;  // Controlled_Buffer controlled_buffer_3
  assign controlled_buffer_1_out = decoder_1_out3 ? D0 : 1'bz;  // Controlled_Buffer controlled_buffer_4
  assign controlled_buffer_5_out = decoder_1_out0 ? in_2 : 1'bz;  // Controlled_Buffer controlled_buffer_5
  assign controlled_buffer_5_out = decoder_1_out1 ? in_6 : 1'bz;  // Controlled_Buffer controlled_buffer_6
  LED led_2 (.in(controlled_buffer_5_out));
  assign controlled_buffer_5_out = decoder_1_out2 ? in_10 : 1'bz;  // Controlled_Buffer controlled_buffer_7
  assign controlled_buffer_5_out = decoder_1_out3 ? in_14 : 1'bz;  // Controlled_Buffer controlled_buffer_8
  assign controlled_buffer_9_out = decoder_1_out0 ? in_3 : 1'bz;  // Controlled_Buffer controlled_buffer_9
  assign controlled_buffer_9_out = decoder_1_out1 ? in_7 : 1'bz;  // Controlled_Buffer controlled_buffer_10
  LED led_3 (.in(controlled_buffer_9_out));
  assign controlled_buffer_9_out = decoder_1_out2 ? in_11 : 1'bz;  // Controlled_Buffer controlled_buffer_11
  assign controlled_buffer_9_out = decoder_1_out3 ? in_15 : 1'bz;  // Controlled_Buffer controlled_buffer_12
  assign controlled_buffer_13_out = decoder_1_out0 ? in_4 : 1'bz;  // Controlled_Buffer controlled_buffer_13
  assign controlled_buffer_13_out = decoder_1_out1 ? in_8 : 1'bz;  // Controlled_Buffer controlled_buffer_14
  LED led_4 (.in(controlled_buffer_13_out));
  assign controlled_buffer_13_out = decoder_1_out2 ? in_12 : 1'bz;  // Controlled_Buffer controlled_buffer_15
  assign controlled_buffer_13_out = decoder_1_out3 ? in_16 : 1'bz;  // Controlled_Buffer controlled_buffer_16

  // Notes on the sheet:
  //   Fig: 4 Bit bus line with three state buffer
endmodule
