// Logisim project 4-bit arithmetic circuit.circ as structural Verilog: 1 circuit, main circuit main
module main (
  input  Cin,
  input  [1:0] A0,
  input  in_3,
  input  B0,
  input  A1,
  input  B1,
  input  A2,
  input  B2,
  input  A3,
  input  B3,
  input  in_11
);

  wire adder_1_cout, adder_1_out, adder_2_cout, adder_2_out, adder_3_cout, adder_3_out, adder_4_cout,
       adder_4_out, multiplexer_1_out, multiplexer_2_out, multiplexer_3_out, multiplexer_4_out, not_1_out,
       not_2_out, not_3_out, not_4_out, not_5_out;

  not not_1 (not_1_out, B0);
  not not_2 (not_2_out, B1);
  not not_3 (not_3_out, B2);
  not not_4 (not_4_out, B3);
  not not_5 (not_5_out, in_11);
  Multiplexer #(.select(2)) multiplexer_1 (
    .in0(B0), .in1(not_1_out), .in2(in_11), .in3(not_5_out), .out(multiplexer_1_out), .sel(A0));  // open: en
  Multiplexer #(.select(2)) multiplexer_2 (
    .in0(B1), .in1(not_2_out), .in2(in_11), .in3(not_5_out), .out(multiplexer_2_out), .sel(A0));  // open: en
  Multiplexer #(.select(2)) multiplexer_3 (
    .in0(B2), .in1(not_3_out), .in2(in_11), .in3(not_5_out), .out(multiplexer_3_out), .sel(A0));  // open: en
  Multiplexer #(.select(2)) multiplexer_4 (
    .in0(B3), .in1(not_4_out), .in2(in_11), .in3(not_5_out), .out(multiplexer_4_out), .sel(A0));  // open: en
  Adder #(.width(1)) adder_1 (.a(in_3), .b(multiplexer_1_out), .out(adder_1_out), .cin(Cin), .cout(adder_1_cout));
  Adder #(.width(1)) adder_2 (
    .a(A1), .b(multiplexer_2_out), .out(adder_2_out), .cin(adder_1_cout), .cout(adder_2_cout));
  Adder #(.width(1)) adder_3 (
    .a(A2), .b(multiplexer_3_out), .out(adder_3_out), .cin(adder_2_cout), .cout(adder_3_cout));
  Adder #(.width(1)) adder_4 (
    .a(A3), .b(multiplexer_4_out), .out(adder_4_out), .cin(adder_3_cout), .cout(adder_4_cout));
  LED led_1 (.in(adder_4_cout));
  LED led_2 (.in(adder_1_out));
  LED led_3 (.in(adder_2_out));
  LED led_4 (.in(adder_3_out));
  LED led_5 (.in(adder_4_out));

  // Notes on the sheet:
  //   S1 S0
  //   D4
  //   D0
  //   D1
  //   D2
  //   D3
endmodule
