// Logisim project Bus system for four registers (2).circ as structural Verilog: 1 circuit, main circuit main
module main (
  input  [1:0] in_1,
  input  in_2,
  input  in_3,
  input  in_4,
  input  in_5,
  input  in_6,
  input  in_7,
  input  in_8,
  input  in_9,
  input  in_10,
  input  in_11,
  input  in_12,
  input  in_13,
  input  in_14,
  input  in_15,
  input  in_16,
  input  in_17
);

  wire multiplexer_1_out, multiplexer_2_out, multiplexer_3_out, multiplexer_4_out;

  Multiplexer #(.select(2)) multiplexer_1 (
    .in0(in_14), .in1(in_10), .in2(in_6), .in3(in_2), .out(multiplexer_1_out), .sel(in_1));  // open: en
  Multiplexer #(.select(2)) multiplexer_2 (
    .in0(in_15), .in1(in_11), .in2(in_7), .in3(in_3), .out(multiplexer_2_out), .sel(in_1));  // open: en
  Multiplexer #(.select(2)) multiplexer_3 (
    .in0(in_16), .in1(in_12), .in2(in_8), .in3(in_4), .out(multiplexer_3_out), .sel(in_1));  // open: en
  Multiplexer #(.select(2)) multiplexer_4 (
    .in0(in_17), .in1(in_13), .in2(in_9), .in3(in_5), .out(multiplexer_4_out), .sel(in_1));  // open: en
  LED led_1 (.in(multiplexer_1_out));
  LED led_2 (.in(multiplexer_2_out));
  LED led_3 (.in(multiplexer_3_out));
  LED led_4 (.in(multiplexer_4_out));

  // Notes on the sheet:
  //   Select Line
  //   Register-D
  //   Register-C
  //   Bus system for four registers
  //   Register-B
  //   Register-A
  //   4 Line Common bus
endmodule
