// Logisim project Computer architechture lab Project.circ as structural Verilog: 1 circuit, main circuit main
module main (
  input  Cin,
  input  [1:0] A0,
  input  in_3,
  input  B0,
  input  A1,
  input  B1,
  input  A2,
  input  B2,
  input  A3,
  input  B3,
  input  in_11,
  input  Control_Unit,
  input  A,
  input  in_14,
  input  A_2,
  input  A_3,
  input  in_17,
  input  A_4,
  input  in_19,
  input  in_20,
  input  B,
  input  B_2,
  input  B_3,
  input  B_4,
  input  in_25,
  input  in_26,
  input  in_27,
  input  [3:0] in_28
);

  wire adder_1_cout, adder_1_out, adder_2_cout, adder_2_out, adder_3_cout, adder_3_out, adder_4_cout,
       adder_4_out, and_1_out, and_2_out, and_3_out, and_4_out, and_5_out, and_6_out, and_7_out, and_8_out,
       and_9_out, and_10_out, and_11_out, and_12_out, buffer_1_out, buffer_2_out, buffer_3_out, buffer_4_out,
       buffer_5_out, buffer_6_out, buffer_7_out, buffer_8_out, buffer_9_out, buffer_10_out, buffer_11_out,
       buffer_12_out, buffer_13_out, buffer_14_out, buffer_15_out, multiplexer_1_out, multiplexer_2_out,
       multiplexer_3_out, multiplexer_4_out, multiplexer_5_out, multiplexer_6_out, multiplexer_7_out,
       multiplexer_8_out, nand_1_out, nand_2_out, nand_3_out, nand_4_out, nor_1_out, nor_2_out, nor_3_out,
       nor_4_out, not_1_out, not_2_out, not_3_out, not_4_out, not_5_out, not_6_out, not_7_out, not_8_out,
       not_9_out, not_10_out, not_11_out, not_12_out, not_13_out, not_14_out, not_15_out, not_16_out,
       not_17_out, not_18_out, not_19_out, not_20_out, not_21_out, not_22_out, not_23_out, not_24_out,
       not_25_out, not_26_out, not_27_out, not_28_out, not_29_out, not_30_out, or_1_out, or_2_out, or_3_out,
       or_4_out, or_5_out, or_6_out, or_7_out, or_8_out, or_9_out, or_10_out, or_11_out, or_12_out,
       xnor_1_out, xnor_2_out, xnor_3_out, xnor_4_out, xor_1_out, xor_2_out, xor_3_out, xor_4_out;

  not not_1 (not_1_out, B0);
  not not_2 (not_2_out, B1);
  not not_3 (not_3_out, B2);
  not not_4 (not_4_out, B3);
  not not_5 (not_5_out, in_11);
  buf buffer_1 (buffer_1_out, in_14);
  not not_6 (not_6_out, B);
  buf buffer_2 (buffer_2_out, A);
  not not_7 (not_7_out, A);
  buf buffer_3 (buffer_3_out, B);
  not not_8 (not_8_out, B);
  not not_9 (not_9_out, B);
  not not_10 (not_10_out, A);
  not not_11 (not_11_out, A);
  buf buffer_4 (buffer_4_out, in_25);
  and and_1 (and_1_out, A, B);
  and and_2 (and_2_out, A, not_6_out);
  and and_3 (and_3_out, not_7_out, B);
  xor xor_1 (xor_1_out, A, B);
  or or_1 (or_1_out, A, B);
  nor nor_1 (nor_1_out, A, B);
  xnor xnor_1 (xnor_1_out, A, B);
  or or_2 (or_2_out, A, not_9_out);
  or or_3 (or_3_out, not_11_out, B);
  nand nand_1 (nand_1_out, A, B);
  Multiplexer #(.select(2)) multiplexer_1 (
    .in0(B0), .in1(not_1_out), .in2(in_11), .in3(not_5_out), .out(multiplexer_1_out), .sel(A0),
    .en(not_12_out));
  Multiplexer #(.select(2)) multiplexer_2 (
    .in0(B1), .in1(not_2_out), .in2(in_11), .in3(not_5_out), .out(multiplexer_2_out), .sel(A0),
    .en(not_12_out));
  Multiplexer #(.select(2)) multiplexer_3 (
    .in0(B2), .in1(not_3_out), .in2(in_11), .in3(not_5_out), .out(multiplexer_3_out), .sel(A0),
    .en(not_12_out));
  Multiplexer #(.select(2)) multiplexer_4 (
    .in0(B3), .in1(not_4_out), .in2(in_11), .in3(not_5_out), .out(multiplexer_4_out), .sel(A0),
    .en(not_12_out));
  not not_12 (not_12_out, Control_Unit);
  Multiplexer #(.select(4)) multiplexer_5 (
    .in0(buffer_1_out), .in1(and_1_out), .in2(and_2_out), .in3(buffer_2_out), .in4(and_3_out),
    .in5(buffer_3_out), .in6(xor_1_out), .in7(or_1_out), .in8(nor_1_out), .in9(xnor_1_out), .in10(not_8_out),
    .in11(or_2_out), .in12(not_10_out), .in13(or_3_out), .in14(nand_1_out), .in15(buffer_4_out),
    .out(multiplexer_5_out), .sel(in_28), .en(Control_Unit));
  Adder #(.width(1)) adder_1 (.a(in_3), .b(multiplexer_1_out), .out(adder_1_out), .cin(Cin), .cout(adder_1_cout));
  Adder #(.width(1)) adder_2 (
    .a(A1), .b(multiplexer_2_out), .out(adder_2_out), .cin(adder_1_cout), .cout(adder_2_cout));
  Adder #(.width(1)) adder_3 (
    .a(A2), .b(multiplexer_3_out), .out(adder_3_out), .cin(adder_2_cout), .cout(adder_3_cout));
  Adder #(.width(1)) adder_4 (
    .a(A3), .b(multiplexer_4_out), .out(adder_4_out), .cin(adder_3_cout), .cout(adder_4_cout));
  LED led_1 (.in(adder_4_cout));
  LED led_2 (.in(adder_1_out));
  LED led_3 (.in(adder_2_out));
  LED led_4 (.in(adder_3_out));
  LED led_5 (.in(adder_4_out));
  not not_13 (not_13_out, B_2);
  buf buffer_5 (buffer_5_out, A_2);
  not not_14 (not_14_out, A_2);
  buf buffer_6 (buffer_6_out, B_2);
  not not_15 (not_15_out, B_2);
  or or_4 (or_4_out, A_2, not_16_out);
  not not_16 (not_16_out, B_2);
  not not_17 (not_17_out, A_2);
  not not_18 (not_18_out, A_2);
  buf buffer_7 (buffer_7_out, in_19);
  and and_4 (and_4_out, A_2, B_2);
  and and_5 (and_5_out, A_2, not_13_out);
  and and_6 (and_6_out, not_14_out, B_2);
  xor xor_2 (xor_2_out, A_2, B_2);
  or or_5 (or_5_out, A_2, B_2);
  nor nor_2 (nor_2_out, A_2, B_2);
  xnor xnor_2 (xnor_2_out, A_2, B_2);
  or or_6 (or_6_out, not_18_out, B_2);
  nand nand_2 (nand_2_out, A_2, B_2);
  buf buffer_8 (buffer_8_out, in_26);
  Multiplexer #(.select(4)) multiplexer_6 (
    .in0(buffer_7_out), .in1(and_4_out), .in2(and_5_out), .in3(buffer_5_out), .in4(and_6_out),
    .in5(buffer_6_out), .in6(xor_2_out), .in7(or_5_out), .in8(nor_2_out), .in9(xnor_2_out),
    .in10(not_15_out), .in11(or_4_out), .in12(not_17_out), .in13(or_6_out), .in14(nand_2_out),
    .in15(buffer_8_out), .out(multiplexer_6_out), .sel(in_28), .en(Control_Unit));
  not not_19 (not_19_out, B_3);
  buf buffer_9 (buffer_9_out, A_3);
  not not_20 (not_20_out, A_3);
  buf buffer_10 (buffer_10_out, B_3);
  not not_21 (not_21_out, B_3);
  not not_22 (not_22_out, B_3);
  not not_23 (not_23_out, A_3);
  not not_24 (not_24_out, A_3);
  buf buffer_11 (buffer_11_out, in_27);
  buf buffer_12 (buffer_12_out, in_17);
  and and_7 (and_7_out, A_3, B_3);
  and and_8 (and_8_out, A_3, not_19_out);
  and and_9 (and_9_out, not_20_out, B_3);
  xor xor_3 (xor_3_out, A_3, B_3);
  or or_7 (or_7_out, A_3, B_3);
  nor nor_3 (nor_3_out, A_3, B_3);
  xnor xnor_3 (xnor_3_out, A_3, B_3);
  or or_8 (or_8_out, A_3, not_22_out);
  or or_9 (or_9_out, not_24_out, B_3);
  nand nand_3 (nand_3_out, A_3, B_3);
  LED led_6 (.in(multiplexer_5_out));
  LED led_7 (.in(multiplexer_6_out));
  Multiplexer #(.select(4)) multiplexer_7 (
    .in0(buffer_12_out), .in1(and_7_out), .in2(and_8_out), .in3(buffer_9_out), .in4(and_9_out),
    .in5(buffer_10_out), .in6(xor_3_out), .in7(or_7_out), .in8(nor_3_out), .in9(xnor_3_out),
    .in10(not_21_out), .in11(or_8_out), .in12(not_23_out), .in13(or_9_out), .in14(nand_3_out),
    .in15(buffer_11_out), .out(multiplexer_7_out), .sel(in_28), .en(Control_Unit));
  LED led_8 (.in(multiplexer_7_out));
  LED led_9 (.in(multiplexer_8_out));
  not not_25 (not_25_out, B_4);
  buf buffer_13 (buffer_13_out, A_4);
  not not_26 (not_26_out, A_4);
  buf buffer_14 (buffer_14_out, B_4);
  not not_27 (not_27_out, B_4);
  not not_28 (not_28_out, B_4);
  not not_29 (not_29_out, A_4);
  not not_30 (not_30_out, A_4);
  and and_10 (and_10_out, A_4, B_4);
  and and_11 (and_11_out, A_4, not_25_out);
  and and_12 (and_12_out, not_26_out, B_4);
  xor xor_4 (xor_4_out, A_4, B_4);
  or or_10 (or_10_out, A_4, B_4);
  nor nor_4 (nor_4_out, A_4, B_4);
  xnor xnor_4 (xnor_4_out, A_4, B_4);
  or or_11 (or_11_out, A_4, not_28_out);
  or or_12 (or_12_out, not_30_out, B_4);
  nand nand_4 (nand_4_out, A_4, B_4);
  buf buffer_15 (buffer_15_out, in_20);
  Multiplexer #(.select(4)) multiplexer_8 (
    .in0(buffer_15_out), .in1(and_10_out), .in2(and_11_out), .in3(buffer_13_out), .in4(and_12_out),
    .in5(buffer_14_out), .in6(xor_4_out), .in7(or_10_out), .in8(nor_4_out), .in9(xnor_4_out),
    .in10(not_27_out), .in11(or_11_out), .in12(not_29_out), .in13(or_12_out), .in14(nand_4_out), .in15(1'b1),
    .out(multiplexer_8_out), .sel(in_28), .en(Control_Unit));

  // Notes on the sheet:
  //   S1 S0
  //   C-out
  //   D0
  //   D1
  //   D2
  //   D3
  //   Arithmetic Circuit
  //   Logic Circuit
  //   D0
  //   D1
  //   D2
  //   D3
endmodule
